# Fritzing sketch AR11_fnd (saved by Fritzing 0.9.3b)
breadboards: 1

parts:
  7_Segment1 = 7 Segment Display
  부품1 = Arduino Uno (Rev3)
  R1 = Resistor [tolerance=±5% resistance=220 package=THT]
  R2 = Resistor [tolerance=±5% resistance=220 package=THT]
  R3 = Resistor [tolerance=±5% resistance=220 package=THT]
  R4 = Resistor [tolerance=±5% resistance=220 package=THT]
  R5 = Resistor [tolerance=±5% resistance=220 package=THT]
  R6 = Resistor [tolerance=±5% resistance=220 package=THT]
  R7 = Resistor [tolerance=±5% resistance=220 package=THT]
  R8 = Resistor [tolerance=±5% resistance=220 package=THT]

nets:
  N1: 7_Segment1.Segment_G, R5.Pin_0
  N2: 7_Segment1.Segment_F, R6.Pin_0
  N3: 7_Segment1.common_anode, 부품1.GND
  N4: 7_Segment1.Segment_E, R8.Pin_1
  N5: 7_Segment1.Segment_D, R7.Pin_1
  N6: 7_Segment1.Segment_DP, R2.Pin_1
  N7: 7_Segment1.Segment_C, R1.Pin_1
  N8: 7_Segment1.Segment_B, R3.Pin_0
  N9: 7_Segment1.Segment_A, R4.Pin_0
  N10: 부품1.D8, R5.Pin_1
  N11: 부품1.D9_PWM, R2.Pin_0
  N12: 부품1.D2, R4.Pin_1
  N13: 부품1.D3_PWM, R3.Pin_1
  N14: 부품1.D4, R1.Pin_0
  N15: 부품1.D5_PWM, R7.Pin_0
  N16: 부품1.D6_PWM, R8.Pin_0
  N17: 부품1.D7, R6.Pin_1
