# Fritzing sketch Untitled Sketch 2 (saved by Fritzing 0.9.3b)
breadboards: 1

parts:
  R1 = PHOTOCELL [package=photocell-kit]
  R2 = Resistor [tolerance=±5% resistance=10k package=THT]
  Generic_4x4_button_keypad1 = Generic 4x4 Keypad
  부품2 = LCD1602-I2C
  HC-SR04_Sensor_1 = HC-SR04 Ultrasonic Distance Sensor
  부품3 = RFID-RC522 [part_number=101218]
  부품4 = Arduino Mega 2560 (Rev3)
  LED1 = smd LED [color="White (6500K)" package="0805 [SMD]"]
  R3 = Resistor [tolerance=±5% resistance=220 package=THT]

nets:
  GND: R1.P$1, 부품2.GND, HC-SR04_Sensor_1.GND, 부품3.GND, 부품4.GND, R3.Pin_1
  N1: R1.P$2, R2.Pin_1, 부품4.A0
  VCC: R2.Pin_0, 부품2.VCC, HC-SR04_Sensor_1.VCC, 부품4.5V
  N2: Generic_4x4_button_keypad1.C4, 부품4.D2_PWM
  N3: Generic_4x4_button_keypad1.C3, 부품4.D3_PWM
  N4: Generic_4x4_button_keypad1.C2, 부품4.D4_PWM
  N5: Generic_4x4_button_keypad1.C1, 부품4.D5_PWM
  N6: Generic_4x4_button_keypad1.R1, 부품4.D6_PWM
  N7: Generic_4x4_button_keypad1.R2, 부품4.D7_PWM
  N8: Generic_4x4_button_keypad1.R3, 부품4.D8_PWM
  N9: Generic_4x4_button_keypad1.R4, 부품4.D9_PWM
  N10: 부품2.SDA, 부품4.D20/SDA
  N11: 부품2.SCL, 부품4.D21/SCL
  N12: HC-SR04_Sensor_1.TRIG, 부품4.D10_PWM
  N13: HC-SR04_Sensor_1.ECHO, 부품4.D11_PWM
  N14: 부품3.SDA, 부품4.D53
  N15: 부품3.SCK, 부품4.D52
  N16: 부품3.MOSI, 부품4.D51
  N17: 부품3.MISO, 부품4.D50
  N18: 부품3.RST, 부품4.D49
  3.3V: 부품3.3.3V, 부품4.3V3
  N19: 부품4.D31, LED1.anode
  N20: LED1.cathode, R3.Pin_0

custom parts:
  Generic 4x4 Keypad: generic 4x4 keypad 4 rows of four 6 mm tact switches cheap and nasty but works
  LCD1602-I2C: A standard character display, usually with 2x16 characters. Comes in many colors with LCM1602 IIC attached.
